# Fritzing sketch tvbgone (saved by Fritzing 0.7.12b)
breadboards: 1

parts:
  ARDUINO1 = Arduino Micro
  S1 = Pushbutton [package="[SMD]"]
  Q1 = NPN-Transistor [package="SOT-23 [SMD]"]
  R1 = 47 Ω Resistor [package=THT]
  LED1 = white smd LED [package="0603 [SMD]"]
  R2 = 68 Ω Resistor [package=THT]

nets:
  N1: ARDUINO1.D2, S1.Pin_3, S1.Pin_4
  N2: ARDUINO1.D3, R1.Pin_0
  N3: ARDUINO1.5V, LED1.anode
  N4: ARDUINO1.GND#31, S1.Pin_1, S1.Pin_2, Q1.2
  N5: Q1.0, R1.Pin_1
  N6: Q1.1, R2.Pin_1
  N7: LED1.cathode, R2.Pin_0

custom parts:
  Arduino Micro: Arduino Micro Microcontroller
